# Fritzing sketch EspressoGuide (saved by Fritzing 0.9.2b)

parts:
  R1 = Resistor [tolerance=±5% resistance=220 package=THT]
  MV1 = MicroView [part_number=MicroView package="16pin wide"]
  Update_IF = female pin header, 5 pins [form="♀ (female)"]
  D1 = Rectifier Diode [part_number=1N4001 package="300 mil [THT]"]
  C1 = Ceramic Capacitor [capacitance=100nF package="100 mil [THT, multilayer]"]
  Power = female pin header, 2 pins [form="♀ (female)"]
  D2 = Rectifier Diode [part_number=1N4001 package="300 mil [THT]"]
  T1 = female pin header, 3 pins [form="♀ (female)"]
  C2 = Ceramic Capacitor [capacitance=100nF package="100 mil [THT, multilayer]"]
  D3 = Rectifier Diode [part_number=1N4001 package="300 mil [THT]"]
  D4 = Rectifier Diode [part_number=1N4001 package="300 mil [THT]"]
  D5 = Rectifier Diode [part_number=1N4001 package="300 mil [THT]"]
  Current_Sensor = female pin header, 2 pins [form="♀ (female)"]
  D6 = Rectifier Diode [part_number=1N4001 package="300 mil [THT]"]
  C3 = Electrolytic Capacitor [capacitance=47µF package="100 mil [THT, electrolytic]"]
  R3 = Resistor [tolerance=±5% resistance=220 package=THT]
  R2 = Resistor [tolerance=±5% resistance=1.5k package=THT]

nets:
  N1: R1.Pin_0, MV1.D2, C2.0
  N2: R1.Pin_1, T1.pin1
  N3: MV1.RESET, C1.0
  N4: MV1.A0, R3.Pin_1
  N5: MV1.GND, Update_IF.pin2, Power.pin2, T1.pin3, C2.1, D3.anode, D4.anode, C3.-, R2.Pin_1
  N6: MV1.RXD, Update_IF.pin4
  N7: MV1.TXD, Update_IF.pin3
  N8: MV1.D3, T1.pin2
  N9: MV1.Vin, D1.cathode, D2.cathode
  N10: Update_IF.pin1, D1.anode
  N11: Update_IF.pin5, C1.1
  N12: Power.pin1, D2.anode
  N13: D3.cathode, D5.anode, Current_Sensor.pin1
  N14: D4.cathode, Current_Sensor.pin2, D6.anode
  N15: D5.cathode, D6.cathode, C3.+, R3.Pin_0, R2.Pin_0

custom parts:
  MicroView: MicroView - Chip-sized Arduino with OLED display.
